// Logisim project digital_clock.circ as structural Verilog: 4 circuits, main circuit main
module main (
  input  in_1
);

  wire and_1_out, and_2_out, and_3_out, and_4_out, CLK, CLK_DIV2, clock_1_out, d_ff_1_qn, HOUR_ADV,
       MANUAL_CLK_out, MIN_ADV, or_1_out, or_2_out, or_3_out, RESET, RUN_nSET, RUN_SET, SET_HOUR, SET_MIN;
  wire [3:0] H0, H1, M0, M1, S0, S1;

  // Digital_Oscilloscope #(.nState(35)) digital_oscilloscope_1: pin names not known; wires that end beside it: CLK, CLK_DIV2, RESET, RUN_SET, RUN_nSET, MIN_ADV, HOUR_ADV
  Button button_1 (.out(RESET));
  _7_Segment_Display u_7_segment_display_1 (.dp(and_1_out));  // open: g, f, a, b, e, d, c
  // BCD_to_7_Segment_decoder bcd_to_7_segment_decoder_1: pin names not known; wires that end beside it: H1
  _7_Segment_Display u_7_segment_display_2 (.dp(and_1_out));  // open: g, f, a, b, e, d, c
  // BCD_to_7_Segment_decoder bcd_to_7_segment_decoder_2: pin names not known; wires that end beside it: H0
  and and_1 (and_1_out, ~RUN_nSET, CLK);  // AND_Gate
  or or_1 (or_1_out, ~RUN_nSET, RESET);  // OR_Gate
  Button #(.press("passive")) button_2 (.out(RUN_SET));
  LED led_1 (.in(and_4_out));
  Button #(.press("passive")) button_3 (.out(SET_HOUR));
  _7_Segment_Display u_7_segment_display_3 (.dp(and_2_out));  // open: g, f, a, b, e, d, c
  // BCD_to_7_Segment_decoder bcd_to_7_segment_decoder_3: pin names not known; wires that end beside it: M1
  LED led_2 (.in(and_4_out));
  Button #(.press("passive")) button_4 (.out(SET_MIN));
  _7_Segment_Display u_7_segment_display_4 (.dp(and_2_out));  // open: g, f, a, b, e, d, c
  // BCD_to_7_Segment_decoder bcd_to_7_segment_decoder_4: pin names not known; wires that end beside it: M0
  and and_2 (and_2_out, ~RUN_nSET, CLK);  // AND_Gate
  or or_2 (or_2_out, SET_MIN, RUN_nSET);
  LED led_3 (.in(and_4_out));
  LED led_4 (.in(and_4_out));
  zero_to_60 zero_to_60_1 (.ADV(CLK), .CLK(CLK), .CLR(or_1_out), .D0(S0), .D1(S1));
  _7_Segment_Display u_7_segment_display_5 (.dp(and_3_out));  // open: g, f, a, b, e, d, c
  // BCD_to_7_Segment_decoder bcd_to_7_segment_decoder_5: pin names not known; wires that end beside it: S1
  xnor xnor_1 (MIN_ADV, S1[2], or_2_out);
  Clock clock_1 (.out(clock_1_out));
  _7_Segment_Display u_7_segment_display_6 (.dp(and_3_out));  // open: g, f, a, b, e, d, c
  // BCD_to_7_Segment_decoder bcd_to_7_segment_decoder_6: pin names not known; wires that end beside it: S0
  and and_3 (and_3_out, ~RUN_nSET, CLK);  // AND_Gate
  Button MANUAL_CLK (.out(MANUAL_CLK_out));
  and and_4 (and_4_out, RUN_nSET, ~CLK_DIV2);  // AND_Gate
  Multiplexer multiplexer_1 (.in0(clock_1_out), .in1(MANUAL_CLK_out), .out(CLK), .sel(in_1));
  zero_to_60 zero_to_60_2 (.ADV(MIN_ADV), .CLK(CLK), .CLR(RESET), .D0(M0), .D1(M1));
  or or_3 (or_3_out, SET_HOUR, RUN_nSET);
  D_Flip_Flop d_ff_1 (.D(d_ff_1_qn), .clk(CLK), .Q(CLK_DIV2), .Qn(d_ff_1_qn));  // open: preset, reset
  xnor xnor_2 (HOUR_ADV, or_3_out, M1[2]);
  J_K_Flip_Flop j_k_ff_1 (.J(1'b1), .K(1'b1), .clk(RUN_SET), .Q(RUN_nSET), .preset(RESET));  // open: Qn, reset
  zero_to_24 zero_to_24_1 (.ADV(HOUR_ADV), .CLK(CLK), .CLR(RESET), .D0(H0), .D1(H1));
endmodule

module up_counter (
  input  CLK,
  input  CLR,
  output [3:0] CNT_OUT
);

  J_K_Flip_Flop #(.trigger("falling")) j_k_ff_1 (
    .J(1'b1), .K(1'b1), .clk(CLK), .Q(CNT_OUT[0]), .reset(CLR));  // open: Qn, preset
  J_K_Flip_Flop #(.trigger("falling")) j_k_ff_2 (
    .J(1'b1), .K(1'b1), .clk(CNT_OUT[0]), .Q(CNT_OUT[1]), .reset(CLR));  // open: Qn, preset
  J_K_Flip_Flop #(.trigger("falling")) j_k_ff_3 (
    .J(1'b1), .K(1'b1), .clk(CNT_OUT[1]), .Q(CNT_OUT[2]), .reset(CLR));  // open: Qn, preset
  J_K_Flip_Flop #(.trigger("falling")) j_k_ff_4 (
    .J(1'b1), .K(1'b1), .clk(CNT_OUT[2]), .Q(CNT_OUT[3]), .reset(CLR));  // open: Qn, preset
endmodule

module zero_to_60 (
  input  ADV,
  input  CLK,
  input  CLR,
  output [3:0] D0,
  output [3:0] D1
);

  wire and_1_out, and_2_out, or_1_out, or_2_out;

  or or_1 (or_1_out, CLR, and_1_out);
  up_counter up_counter_1 (.CLK(ADV), .CLR(or_1_out), .CNT_OUT(D0));
  or or_2 (or_2_out, CLR, and_2_out);
  and and_1 (and_1_out, D0[3], D0[1], ~CLK);  // AND_Gate
  up_counter up_counter_2 (.CLK(D0[3]), .CLR(or_2_out), .CNT_OUT(D1));
  and and_2 (and_2_out, ~CLK, D1[2], D1[1]);  // AND_Gate
endmodule

module zero_to_24 (
  input  ADV,
  input  CLK,
  input  CLR,
  output [3:0] D0,
  output [3:0] D1
);

  wire and_1_out, and_2_out, and_3_out, and_4_out, and_5_out, or_1_out, or_2_out, or_3_out, or_4_out;

  and and_1 (and_1_out, D0[2], D1[1]);
  and and_2 (and_2_out, D1[1], ~CLK, D1[0]);  // AND_Gate
  or or_1 (or_1_out, CLR, and_5_out);
  or or_2 (or_2_out, D0[3], and_1_out);
  or or_3 (or_3_out, CLR, and_2_out);
  up_counter up_counter_1 (.CLK(ADV), .CLR(or_1_out), .CNT_OUT(D0));
  up_counter up_counter_2 (.CLK(or_2_out), .CLR(or_3_out), .CNT_OUT(D1));
  and and_3 (and_3_out, D0[2], D1[1]);
  and and_4 (and_4_out, ~D1[1], D0[1], D0[3]);  // AND_Gate
  or or_4 (or_4_out, and_3_out, and_4_out);
  and and_5 (and_5_out, or_4_out, ~CLK);  // AND_Gate
endmodule
